# Fritzing sketch watchwinder (saved by Fritzing 0.9.3b)

parts:
  28BYJ-48_ULN2003_Stepper_Motor_5V = 28BYJ-48 Stepper Motor
  X1 = X113647 Stepper Driver Board [part_number=X113647 package=board]
  Lolin_D1_Mini_v3_1 = WeMos D1 Mini
  C1 = Capacitor Polarized [package=panasonic_d]
  SSD1306_OLED_0_96"_I2C_5V = OLED 128x64 I2C Monochrome Display

nets:
  N1: 28BYJ-48_ULN2003_Stepper_Motor_5V.BLUE, X1.BLUE
  N2: 28BYJ-48_ULN2003_Stepper_Motor_5V.PINK, X1.PINK
  N3: 28BYJ-48_ULN2003_Stepper_Motor_5V.RED, X1.RED
  N4: 28BYJ-48_ULN2003_Stepper_Motor_5V.ORANGE, X1.ORANGE
  N5: 28BYJ-48_ULN2003_Stepper_Motor_5V.YELLOW, X1.YELLOW
  N6: X1.IN1, Lolin_D1_Mini_v3_1.D5
  N7: X1.IN2, Lolin_D1_Mini_v3_1.D6
  N8: X1.IN3, Lolin_D1_Mini_v3_1.D7
  N9: X1.IN4, Lolin_D1_Mini_v3_1.D8
  GND: X1.GND, C1.-
  HVCC: X1.+V, C1.+
  N10: Lolin_D1_Mini_v3_1.D1, SSD1306_OLED_0_96"_I2C_5V.SDA
  N11: Lolin_D1_Mini_v3_1.D2, SSD1306_OLED_0_96"_I2C_5V.SCK

notes:
  Smart Watch Winder by
  Davide Perini

custom parts:
  28BYJ-48 Stepper Motor: 28BYJ-48 gear-reduction stepper motor (small)
  X113647 Stepper Driver Board: A common stepper motor driver board based on ULN2003APG darlington array
